# Fritzing sketch ArduinoNanoTester (saved by Fritzing 0.9.3b)
circuit board: 8.46667cm x 5.64444cm

parts:
  Stepper_Driver = DRV 8825 Stepper Motor Carrier, High Current [part_number="DRV 8825"]
  Arduino_Nano = Arduino Nano (Rev3.0)
  24V_+_- = Screw terminal - 2 pins [package=THT]
  47uF = Electrolytic Capacitor [capacitance=47µF voltage=50V package="100 mil [THT, electrolytic]"]
  Potentiometer = Rotary Potentiometer (Large) [maximum_resistance=100kΩ package=THT]
  Motor = Stepper Motor - Bipolar
  DC-DC_Converter = Mini-360 DC-DC Buck converter [package=THT]
  MS0 = male pin header, 2 pins [form="♂ (male)"]
  MS2 = male pin header, 2 pins [form="♂ (male)"]
  MS1 = male pin header, 2 pins [form="♂ (male)"]
  Direction_Button = Pushbutton [package="[THT]"]
  Pull-up = Resistor [tolerance=±5% resistance=10k package=THT]

nets:
  N1: Stepper_Driver.ENABLE, Arduino_Nano.D4
  N2: Stepper_Driver.MS1, MS0.pin2
  N3: Stepper_Driver.MS2, MS1.pin2
  N4: Stepper_Driver.MS3, MS2.pin2
  N5: Stepper_Driver.RESET, Arduino_Nano.D7
  N6: Stepper_Driver.SLEEP, Arduino_Nano.D6
  N7: Stepper_Driver.STEP, Arduino_Nano.D3
  N8: Stepper_Driver.DIRECTION, Arduino_Nano.D2
  N9: Stepper_Driver.VOLTAGE_ST/_MT, 24V_+_-.pin2, 47uF.+, DC-DC_Converter.IN+
  N10: Stepper_Driver.GROUND_ST/_MT, Stepper_Driver.GROUND_LOG, Arduino_Nano.GND, 24V_+_-.pin1, 47uF.-, Potentiometer.leg1, DC-DC_Converter.IN-, DC-DC_Converter.OUT-, Direction_Button.Pin_1, Direction_Button.Pin_2
  N11: Stepper_Driver.OUT_2B, Motor.D
  N12: Stepper_Driver.OUT_2A, Motor.B
  N13: Stepper_Driver.OUT_1A, Motor.A
  N14: Stepper_Driver.OUT_1B, Motor.C
  N15: Stepper_Driver.VOLTAGE_DD, Arduino_Nano.5V, Potentiometer.leg2, MS0.pin1, MS2.pin1, MS1.pin1, Pull-up.Pin_1
  N16: Arduino_Nano.D5, Direction_Button.Pin_3, Direction_Button.Pin_4, Pull-up.Pin_0
  N17: Arduino_Nano.VIN, DC-DC_Converter.OUT+
  N18: Arduino_Nano.A0, Potentiometer.wiper

custom parts:
  Mini-360 DC-DC Buck converter: Mini-360 DC-DC Buck converter. Tiny buck step down voltage converter, input voltage 4.75 to 23V output 1 to 17V adjustable. Available from ebay and the like.
